// Logisim project NARCY.circ as structural Verilog: 3 circuits, main circuit main
module main (
);

  wire clk_GPR_A, clk_GPR_B, clk_GPR_C, clk_IR, clk_PC, clk_RAM_ADDR, clk_RAM_DATA, flg_GPR_A_WRITE,
       flg_GPR_B_WRITE, flg_GPR_C_WRITE, flg_IR_WRITE, flg_RAM_ADDR_WRITE, flg_RAM_WRITE, inc_PC, rst_PC;
  wire [7:0] GPR_A_DATA, GPR_A_q, GPR_B_DATA, GPR_B_q, GPR_C_DATA, GPR_C_q, IR_DATA, IR_q, PC_DATA, RAM_DATA,
       registerreadwriteprotection_1_registerin, registerreadwriteprotection_2_registerin,
       registerreadwriteprotection_3_registerin, registerreadwriteprotection_4_registerin;
  wire [15:0] AR_q, RAM_ADDR, registerreadwriteprotection16bit_1_dout,
       registerreadwriteprotection16bit_1_registerin;

  // Probe on registerreadwriteprotection16bit_1_dout
  Register #(.width(16)) AR (
    .D(registerreadwriteprotection16bit_1_registerin), .Q(AR_q), .clk(clk_RAM_ADDR));  // open: en, clr
  RegisterReadWriteProtection16bit registerreadwriteprotection16bit_1 (
    .RegisterIn(registerreadwriteprotection16bit_1_registerin),
    .Dout(registerreadwriteprotection16bit_1_dout), .RegisterOut(AR_q), .write(flg_RAM_ADDR_WRITE),
    .Din(RAM_ADDR));
  RAM #(.addrWidth(16), .enables("line")) ram_1 (
    .addr(registerreadwriteprotection16bit_1_dout), .we(flg_RAM_WRITE), .clk(clk_RAM_DATA), .din(RAM_DATA),
    .dout(RAM_DATA));
  Counter PC (.load(clk_PC), .D(PC_DATA), .clk(inc_PC), .clr(rst_PC));  // open: count, Q, carry, up
  // Probe on RAM_DATA
  Register IR (.D(registerreadwriteprotection_1_registerin), .Q(IR_q), .clk(clk_IR));  // open: en, clr
  RegisterReadWriteProtection registerreadwriteprotection_1 (
    .RegisterIn(registerreadwriteprotection_1_registerin), .write(flg_IR_WRITE), .Din(IR_DATA),
    .RegisterOut(IR_q));  // open: Dout
  Register GPR_A (.D(registerreadwriteprotection_2_registerin), .Q(GPR_A_q), .clk(clk_GPR_A));  // open: en, clr
  RegisterReadWriteProtection registerreadwriteprotection_2 (
    .RegisterIn(registerreadwriteprotection_2_registerin), .write(flg_GPR_A_WRITE), .Din(GPR_A_DATA),
    .RegisterOut(GPR_A_q));  // open: Dout
  Register GPR_B (.D(registerreadwriteprotection_3_registerin), .Q(GPR_B_q), .clk(clk_GPR_B));  // open: en, clr
  RegisterReadWriteProtection registerreadwriteprotection_3 (
    .RegisterIn(registerreadwriteprotection_3_registerin), .write(flg_GPR_B_WRITE), .Din(GPR_B_DATA),
    .RegisterOut(GPR_B_q));  // open: Dout
  Register GPR_C (.D(registerreadwriteprotection_4_registerin), .Q(GPR_C_q), .clk(clk_GPR_C));  // open: en, clr
  RegisterReadWriteProtection registerreadwriteprotection_4 (
    .RegisterIn(registerreadwriteprotection_4_registerin), .write(flg_GPR_C_WRITE), .Din(GPR_C_DATA),
    .RegisterOut(GPR_C_q));  // open: Dout
endmodule

module RegisterReadWriteProtection (
  input  [7:0] RegisterOut,
  input  write,
  input  [7:0] Din,
  output [7:0] Dout,
  output [7:0] RegisterIn
);

  wire not_1_out;

  not not_1 (not_1_out, write);
  assign RegisterIn = not_1_out ? RegisterOut : 8'bz;  // Controlled_Buffer controlled_buffer_1
  assign RegisterIn = write ? Din : 8'bz;  // Controlled_Buffer controlled_buffer_2

  assign Dout = RegisterOut;

  // Notes on the sheet:
  //   write: pull=down
endmodule

module RegisterReadWriteProtection16bit (
  input  [15:0] RegisterOut,
  input  write,
  input  [15:0] Din,
  output [15:0] Dout,
  output [15:0] RegisterIn
);

  wire not_1_out;

  assign RegisterIn = not_1_out ? RegisterOut : 16'bz;  // Controlled_Buffer controlled_buffer_1
  not not_1 (not_1_out, write);
  assign RegisterIn = write ? Din : 16'bz;  // Controlled_Buffer controlled_buffer_2

  assign Dout = RegisterOut;

  // Notes on the sheet:
  //   write: pull=down
endmodule
